// Logisim project practica04.circ as structural Verilog: 10 circuits, main circuit SUMADOR (1 Bit)
module SUMADOR__1_Bit (
  input  x,
  input  y,
  input  Cin,
  output Suma,
  output Acarreo_o_Cout
);

  wire and_1_out, and_2_out, xor_1_out;

  xor xor_1 (xor_1_out, x, y);
  and and_1 (and_1_out, xor_1_out, Cin);
  and and_2 (and_2_out, x, y);
  xor xor_2 (Suma, xor_1_out, Cin);
  or or_1 (Acarreo_o_Cout, and_1_out, and_2_out);

  // Notes on the sheet:
  //   Sumador de 1 bit
endmodule

module SUMADOR__8_Bits (
  input  [7:0] A,
  input  [7:0] B,
  input  Cin,
  output [7:0] out_4,
  output Cout
);

  wire sumador_1_bit_1_acarreo_o_cout, sumador_1_bit_2_acarreo_o_cout, sumador_1_bit_3_acarreo_o_cout,
       sumador_1_bit_4_acarreo_o_cout, sumador_1_bit_5_acarreo_o_cout, sumador_1_bit_6_acarreo_o_cout,
       sumador_1_bit_7_acarreo_o_cout;

  SUMADOR__1_Bit sumador_1_bit_1 (
    .x(A[0]), .y(B[0]), .Cin(Cin), .Suma(out_4[0]), .Acarreo_o_Cout(sumador_1_bit_1_acarreo_o_cout));
  SUMADOR__1_Bit sumador_1_bit_2 (
    .x(A[1]), .y(B[1]), .Cin(sumador_1_bit_1_acarreo_o_cout), .Suma(out_4[1]),
    .Acarreo_o_Cout(sumador_1_bit_2_acarreo_o_cout));
  SUMADOR__1_Bit sumador_1_bit_3 (
    .x(A[2]), .y(B[2]), .Cin(sumador_1_bit_2_acarreo_o_cout), .Suma(out_4[2]),
    .Acarreo_o_Cout(sumador_1_bit_3_acarreo_o_cout));
  SUMADOR__1_Bit sumador_1_bit_4 (
    .x(A[3]), .y(B[3]), .Cin(sumador_1_bit_3_acarreo_o_cout), .Suma(out_4[3]),
    .Acarreo_o_Cout(sumador_1_bit_4_acarreo_o_cout));
  SUMADOR__1_Bit sumador_1_bit_5 (
    .x(A[4]), .y(B[4]), .Cin(sumador_1_bit_4_acarreo_o_cout), .Suma(out_4[4]),
    .Acarreo_o_Cout(sumador_1_bit_5_acarreo_o_cout));
  SUMADOR__1_Bit sumador_1_bit_6 (
    .x(A[5]), .y(B[5]), .Cin(sumador_1_bit_5_acarreo_o_cout), .Suma(out_4[5]),
    .Acarreo_o_Cout(sumador_1_bit_6_acarreo_o_cout));
  SUMADOR__1_Bit sumador_1_bit_7 (
    .x(A[6]), .y(B[6]), .Cin(sumador_1_bit_6_acarreo_o_cout), .Suma(out_4[6]),
    .Acarreo_o_Cout(sumador_1_bit_7_acarreo_o_cout));
  SUMADOR__1_Bit sumador_1_bit_8 (
    .x(A[7]), .y(B[7]), .Cin(sumador_1_bit_7_acarreo_o_cout), .Suma(out_4[7]), .Acarreo_o_Cout(Cout));

  // Notes on the sheet:
  //   SUMADOR DE 8 BITS
  //   +
  //   sumador 1
  //   sumador 2
  //   sumador 3
  //   sumador 4
  //   sumador 5
  //   sumador 6
  //   sumador 7
  //   sumador 8
endmodule

// D
module RESTADOR__8_Bits (
  input  [7:0] x,
  input  [7:0] y,
  output [7:0] Resultado,
  output Desborde
);

  wire [7:0] negador_8_bits_1_s, sumador_8_bits_1_out_4;

  NEGADOR__8_Bits negador_8_bits_1 (.x(y), .s(negador_8_bits_1_s));
  SUMADOR__8_Bits sumador_8_bits_1 (
    .A(x), .B(negador_8_bits_1_s), .Cin(1'b0), .out_4(sumador_8_bits_1_out_4));  // open: Cout
  SUMADOR__8_Bits sumador_8_bits_2 (
    .A(sumador_8_bits_1_out_4), .B(8'h1), .Cin(1'b0), .out_4(Resultado), .Cout(Desborde));

  // Notes on the sheet:
  //   Representamos el resultado en 8 bits
  //   ya que el resultado de la resta de dos
  //   numeros de 8 bits nunca superara los
  //   8 bits, i.e. nunca habra un desbordamiento
  //   RESTADOR DE 8 BITS
  //   Complemento
  //   Sumador
  //   Sumador
endmodule

module AND__1_Bit (
  input  x,
  input  y,
  output s
);

  and and_1 (s, x, y);

  // Notes on the sheet:
  //   AND DE 1 BIT
endmodule

module AND__8_Bits (
  input  [7:0] x,
  input  [7:0] y,
  output [7:0] s
);

  AND__1_Bit and_1_bit_1 (.x(x[0]), .y(y[0]), .s(s[0]));
  AND__1_Bit and_1_bit_2 (.x(x[1]), .y(y[1]), .s(s[1]));
  AND__1_Bit and_1_bit_3 (.x(x[2]), .y(y[2]), .s(s[2]));
  AND__1_Bit and_1_bit_4 (.x(x[3]), .y(y[3]), .s(s[3]));
  AND__1_Bit and_1_bit_5 (.x(x[4]), .y(y[4]), .s(s[4]));
  AND__1_Bit and_1_bit_6 (.x(x[5]), .y(y[5]), .s(s[5]));
  AND__1_Bit and_1_bit_7 (.x(x[6]), .y(y[6]), .s(s[6]));
  AND__1_Bit and_1_bit_8 (.x(x[7]), .y(y[7]), .s(s[7]));

  // Notes on the sheet:
  //   AND DE 8 BITS
endmodule

module OR__8_BIts (
  input  [7:0] x,
  input  [7:0] y,
  output [7:0] s
);

  or or_1 (s[0], x[0], y[0]);
  or or_2 (s[1], x[1], y[1]);
  or or_3 (s[2], x[2], y[2]);
  or or_4 (s[3], x[3], y[3]);
  or or_5 (s[4], x[4], y[4]);
  or or_6 (s[5], x[5], y[5]);
  or or_7 (s[6], x[6], y[6]);
  or or_8 (s[7], x[7], y[7]);

  // Notes on the sheet:
  //   OR DE 8 BITS
endmodule

module NEGADOR__8_Bits (
  input  [7:0] x,
  output [7:0] s
);

  not not_1 (s[0], x[0]);
  not not_2 (s[1], x[1]);
  not not_3 (s[2], x[2]);
  not not_4 (s[3], x[3]);
  not not_5 (s[4], x[4]);
  not not_6 (s[5], x[5]);
  not not_7 (s[6], x[6]);
  not not_8 (s[7], x[7]);

  // Notes on the sheet:
  //   NEGADOR DE 8 BITS
endmodule

module IGUALDAD__8_BIts (
  input  [7:0] x,
  input  [7:0] y,
  output [7:0] out_3,
  output desborde,
  output x__y
);

  wire [7:0] restador_8_bits_1_resultado;

  RESTADOR__8_Bits restador_8_bits_1 (.x(x), .y(y), .Resultado(restador_8_bits_1_resultado), .Desborde(desborde));
  NEGADOR__8_Bits negador_8_bits_1 (.x(restador_8_bits_1_resultado), .s(out_3));
  and and_1 (x__y, out_3[0], out_3[1], out_3[2], out_3[3], out_3[4], out_3[5], out_3[6], out_3[7]);

  // Notes on the sheet:
  //   IGUALDAD DE 8 BITS
endmodule

module COMPARADOR__8_Bits (
  input  [7:0] x,
  input  [7:0] y,
  output [7:0] out_3,
  output desborde,
  output x_y
);

  RESTADOR__8_Bits restador_8_bits_1 (.x(x), .y(y), .Resultado(out_3), .Desborde(desborde));

  assign x_y = out_3[7];

  // Notes on the sheet:
  //   COMPARADOR DE 8 BITS
endmodule

module ALU__8_Bits (
  input  [7:0] x,
  input  [2:0] Selector,
  input  [7:0] y,
  output [7:0] Resultado,
  output Desborde___Resultado_Igualdad_y_Comparador
);

  wire comparador_8_bits_1_x_y, igualdad_8_bits_1_x__y, restador_8_bits_1_desborde, sumador_8_bits_1_cout;
  wire [7:0] and_8_bits_1_s, comparador_8_bits_1_out_3, igualdad_8_bits_1_out_3, or_8_bits_1_s,
       restador_8_bits_1_resultado, sumador_8_bits_1_out_4;

  AND__8_Bits and_8_bits_1 (.x(x), .y(y), .s(and_8_bits_1_s));
  OR__8_BIts or_8_bits_1 (.x(x), .y(y), .s(or_8_bits_1_s));
  SUMADOR__8_Bits sumador_8_bits_1 (
    .A(x), .B(y), .Cin(1'b0), .out_4(sumador_8_bits_1_out_4), .Cout(sumador_8_bits_1_cout));
  RESTADOR__8_Bits restador_8_bits_1 (
    .x(x), .y(y), .Resultado(restador_8_bits_1_resultado), .Desborde(restador_8_bits_1_desborde));
  IGUALDAD__8_BIts igualdad_8_bits_1 (
    .x(x), .y(y), .out_3(igualdad_8_bits_1_out_3), .x__y(igualdad_8_bits_1_x__y));  // open: desborde
  COMPARADOR__8_Bits comparador_8_bits_1 (
    .x(x), .y(y), .out_3(comparador_8_bits_1_out_3), .x_y(comparador_8_bits_1_x_y));  // open: desborde
  Multiplexer #(.select(3), .width(8), .enable("false")) multiplexer_1 (
    .in0(and_8_bits_1_s), .in1(or_8_bits_1_s), .in2(sumador_8_bits_1_out_4),
    .in3(restador_8_bits_1_resultado), .in4(igualdad_8_bits_1_out_3), .in5(comparador_8_bits_1_out_3),
    .out(Resultado), .sel(Selector));  // open: in6, in7
  Multiplexer #(.select(3), .enable("false")) multiplexer_2 (
    .in2(sumador_8_bits_1_cout), .in3(restador_8_bits_1_desborde), .in4(igualdad_8_bits_1_x__y),
    .in5(comparador_8_bits_1_x_y), .out(Desborde___Resultado_Igualdad_y_Comparador), .sel(Selector));  // open: in0, in1, in6, in7

  // Notes on the sheet:
  //   ALU DE 8 BITS
  //   And
  //   Or
  //   Sumador
  //   Restador
  //   Igualdad
  //   x == y
  //   Comparador
  //   x < y
  //   Codigo de Operacion    Operacion
  //   000
  //   001
  //   010
  //   011
  //   100
  //   101
  //   And
  //   Or
  //   Sumador
  //   Restador
  //   Igualdad
  //   Comparador
endmodule
